# Fritzing sketch Amoxtli-Jap (saved by Fritzing 1.0.2b)

parts:
  Componente1 = InvenSense MPU6050
  A1 = NEO-6M GPS Module [part_number=GY-GPS6MV2]
  J1 = Piezo Speaker
  S1 = Pushbutton [package="[SMD]"]
  M1 = DOIT Esp32 DevKit v1 (30 pins long, 11 pins width) [part_number=ESP32S-PIN30]

nets:
  VCC: Componente1.VCC, A1.Vcc, M1.3V3
  GND: Componente1.GND, A1.GND, J1.pin1, S1.Pin_1, S1.Pin_2, M1.GND
  N1: Componente1.SCL, M1.D22
  N2: Componente1.SDA, M1.D21
  N3: A1.Tx, M1.RX2
  N4: A1.Rx, M1.TX2
  N5: J1.pin2, M1.D5
  N6: S1.Pin_3, S1.Pin_4, M1.D18

custom parts:
  NEO-6M GPS Module: GY-GPS6MV2 NEO-6M GPS Module Module based on U-blox NEO-6M GPS engine, incorporating regulator for 3.3-5V DC input, MS621FE-compatible rechargeable battery for backup and EEPROM for storing configuration settings. Links: NEO-6 series product information page NEO-6 Datasheet
  DOIT Esp32 DevKit v1 (30 pins long, 11 pins width): The DOIT Esp32 DevKit v1 is one of the development board created by DOIT to evaluate the ESP-WROOM-32 module. It is based on the ESP32 microcontroller that boasts Wifi, Bluetooth, Ethernet and Low Power support all in a single chip. (vanepp) made breadboard work, adjusted pin numbering and labels and reduced size of schematic and cleaned up pcb. This chip is 30pins long (2 x15) and 11 pins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
